# Fritzing sketch crystal-circuit-board (saved by Fritzing 0.9.3b)
circuit board: 3.90102cm x 4.34368cm
breadboards: 1

parts:
  R1 = Resistor [tolerance=±5% resistance=300 package=THT]
  Arduino_Nano = Arduino Nano (Rev3.0)
  U1 = mystery part, 3 pins [chip_label=?]

nets:
  N1: R1.Pin_0, U1.pin2
  N2: R1.Pin_1, Arduino_Nano.D4
  N3: Arduino_Nano.GND, U1.pin3
  N4: Arduino_Nano.5V, U1.pin1

notes:
  RBJCE
